# Fritzing sketch Platine (saved by Fritzing 0.9.3b)
circuit board: 8.46667cm x 5.64444cm
perfboards: 1

parts:
  C1 = Electrolytic Capacitor [capacitance=10µF package="100 mil [THT, electrolytic]"]
  Teensy_3_1 = Teensy 3.1
  Bauteil1 = Arduino Pro Mini v13
  Potentiometer = Rotary Potentiometer (Small) [maximum_resistance=100kΩ package=THT]
  Power_Input = screw terminal, 2 pins
  Audio_Input = screw terminal, 2 pins
  i2c_Pullup = Resistor [tolerance=±5% resistance=4.7k package=THT]
  i2c_Pullup_2 = Resistor [tolerance=±5% resistance=4.7k package=THT]
  R2 = Resistor [tolerance=±5% resistance=10k package=THT]
  LED_Data = Screw terminal - 2 pins [package=THT]
  R3 = Resistor [tolerance=±5% resistance=2.2k package=THT]
  C2 = Electrolytic Capacitor [capacitance=10µF package="100 mil [THT, electrolytic]"]
  R1 = Resistor [tolerance=±5% resistance=47k package=THT]

nets:
  N1: C1.-, Audio_Input.pin2
  N2: C1.+, Teensy_3_1.A1/D15, R1.Pin_1
  GND: Teensy_3_1.GND, Bauteil1.GND, Potentiometer.leg2, Power_Input.pin1, LED_Data.pin1
  N3: Teensy_3_1.A4/D18, Bauteil1.A4, i2c_Pullup_2.Pin_0
  N4: Teensy_3_1.A5/D19, Bauteil1.A5, i2c_Pullup.Pin_0
  N5: Teensy_3_1.AGND, Audio_Input.pin1, R3.Pin_0, C2.-
  VIN: Teensy_3_1.Vin, Bauteil1.VCC, Potentiometer.leg1, Power_Input.pin2, i2c_Pullup.Pin_1, i2c_Pullup_2.Pin_1, R2.Pin_1
  N6: Bauteil1.A1, Potentiometer.wiper
  N7: Bauteil1.D4, LED_Data.pin2
  N8: R2.Pin_0, R3.Pin_1, C2.+, R1.Pin_0
